# Fritzing sketch Etape02 (saved by Fritzing 0.9.3b)
breadboards: 1

parts:
  Composant1 = Arduino Nano (Rev3.0)
  LED1 = LED - 3mm [color="Red (633nm)" package="3 mm [THT]"]
  R1 = Resistor [tolerance=±5% resistance=220 package="0402 [SMD]"]

nets:
  N1: Composant1.GND, LED1.cathode
  N2: Composant1.D13/SCK, R1.Pin_0
  N3: LED1.anode, R1.Pin_1
