# Fritzing sketch Etape06 (saved by Fritzing 0.9.3b)
breadboards: 1

parts:
  Composant1 = Arduino Nano (Rev3.0)
  J1 = Piezo Speaker

nets:
  N1: Composant1.GND, J1.pin1
  N2: Composant1.D9, J1.pin2
