# Fritzing sketch Etape07 (saved by Fritzing 0.9.3b)
breadboards: 1

parts:
  Composant1 = Arduino Nano (Rev3.0)
  LED1 = LED - 3mm [color="Red (633nm)" package="3 mm [THT]"]
  R1 = Resistor [tolerance=±5% resistance=220 package="0402 [SMD]"]
  LED2 = LED - 3mm [color="Yellow (595nm)" package="3 mm [THT]"]
  LED3 = LED - 3mm [color="Green (560nm)" package="3 mm [THT]"]

nets:
  N1: Composant1.GND, R1.Pin_0
  N2: Composant1.D10, LED3.anode
  N3: Composant1.D11/MOSI, LED2.anode
  N4: Composant1.D12/MISO, LED1.anode
  N5: LED1.cathode, R1.Pin_1, LED3.cathode
