# Fritzing sketch Etape08 (saved by Fritzing 0.9.3b)
breadboards: 1

parts:
  Composant1 = Arduino Nano (Rev3.0)
  R1 = Resistor [tolerance=±5% resistance=220 package=THT]
  R2 = Resistor [tolerance=±5% resistance=220 package=THT]
  R3 = Resistor [tolerance=±5% resistance=220 package=THT]
  LED1 = RGB LED (com. cathode, rgb) [package="5 mm [THT]"]

nets:
  N1: Composant1.GND, LED1.common_cathode
  N2: Composant1.D9, R3.Pin_0
  N3: Composant1.D10, R2.Pin_0
  N4: Composant1.D11/MOSI, R1.Pin_0
  N5: R1.Pin_1, LED1.red_anode
  N6: R2.Pin_1, LED1.green_anode
  N7: R3.Pin_1, LED1.blue_anode
