# Fritzing sketch Etape11 (saved by Fritzing 0.9.3b)
breadboards: 1

parts:
  Composant1 = Arduino Nano (Rev3.0)
  S1 = Round Pushbutton
  R1 = Resistor [tolerance=±5% resistance=220 package="0402 [SMD]"]

nets:
  N1: Composant1.GND, R1.Pin_1
  N2: Composant1.D2, S1.leg0, R1.Pin_0
  N3: Composant1.5V, S1.leg1
