# Fritzing sketch Etape01 (saved by Fritzing 0.9.3b)
breadboards: 1

parts:
  Composant1 = Arduino Nano (Rev3.0)
  Composant2 = RFID-RC522-v3

nets:
  GND: Composant1.GND, Composant2.GND
  N1: Composant1.D9, Composant2.RST
  N2: Composant1.D10, Composant2.SDA
  N3: Composant1.D11/MOSI, Composant2.MOSI
  N4: Composant1.D12/MISO, Composant2.MISO
  3V3: Composant1.3V3, Composant2.3.3V
  N5: Composant1.D13/SCK, Composant2.SCK

custom parts:
  RFID-RC522-v3: A simple China made RFID-RC522 Reader (6x4 cm); do check the pin labels, as this is a MFRC522 based clone.
